// Logisim project control-logic.circ as structural Verilog: 1 circuit, main circuit control_logic
module control_logic (
  input  [31:0] inst,
  input  BrEq,
  input  BrLt,
  output PCSel,
  output RegWEn,
  output [2:0] ImmSel,
  output BrUn,
  output ASel,
  output BSel,
  output [3:0] ALUSel,
  output MemRW,
  output [1:0] WBSel,
  output CSRSel,
  output CSRWen
);

  wire and_1_out, and_2_out, and_3_out, and_4_out, and_5_out, and_6_out, and_7_out, and_8_out, and_11_out,
       and_14_out, and_15_out, and_16_out, and_17_out, and_18_out, and_19_out, and_20_out, and_21_out,
       and_22_out, and_23_out, and_24_out, and_25_out, and_26_out, and_27_out, and_28_out, and_29_out,
       and_30_out, and_31_out, and_32_out, and_33_out, and_34_out, and_35_out, and_37_out, and_38_out,
       and_39_out, and_40_out, and_41_out, and_42_out, and_43_out, and_44_out, and_45_out, and_46_out,
       and_47_out, and_48_out, and_50_out, and_51_out, and_52_out, comparator_1_eq, comparator_2_eq,
       comparator_5_eq, comparator_6_eq, comparator_8_eq, comparator_9_eq, comparator_10_eq,
       comparator_11_eq, comparator_12_eq, comparator_13_eq, comparator_14_eq, comparator_15_eq,
       comparator_16_eq, comparator_17_eq, comparator_18_eq, comparator_19_eq, comparator_20_eq,
       comparator_21_eq, comparator_22_eq, comparator_23_eq, comparator_24_eq, comparator_25_eq,
       comparator_26_eq, comparator_27_eq, comparator_28_eq, comparator_29_eq, comparator_30_eq,
       comparator_31_eq, comparator_32_eq, comparator_33_eq, comparator_34_eq, comparator_35_eq,
       comparator_36_eq, comparator_37_eq, comparator_38_eq, comparator_39_eq, comparator_40_eq,
       comparator_41_eq, comparator_42_eq, comparator_43_eq, comparator_44_eq, comparator_45_eq,
       comparator_46_eq, comparator_47_eq, comparator_48_eq, comparator_49_eq, comparator_50_eq,
       comparator_51_eq, comparator_52_eq, comparator_53_eq, comparator_54_eq, comparator_55_eq,
       comparator_56_eq, comparator_57_eq, comparator_58_eq, comparator_59_eq, comparator_60_eq,
       comparator_61_eq, comparator_62_eq, comparator_63_eq, comparator_64_eq, comparator_65_eq,
       comparator_66_eq, comparator_67_eq, comparator_68_eq, comparator_69_eq, comparator_70_eq,
       comparator_71_eq, comparator_72_eq, comparator_73_eq, comparator_74_eq, comparator_75_eq,
       comparator_76_eq, comparator_77_eq, comparator_78_eq, comparator_79_eq, comparator_80_eq,
       comparator_81_eq, comparator_82_eq, comparator_83_eq, comparator_84_eq, comparator_85_eq,
       comparator_86_eq, comparator_87_eq, comparator_88_eq, comparator_89_eq, comparator_90_eq,
       comparator_91_eq, comparator_92_eq, comparator_93_eq, comparator_94_eq, comparator_95_eq,
       comparator_96_eq, comparator_97_eq, comparator_98_eq, comparator_99_eq, comparator_100_eq,
       comparator_101_eq, comparator_102_eq, comparator_103_eq, comparator_104_eq, is_add, is_and, is_bsel,
       is_mul, is_mulh, is_mulhu, is_or, is_sll, is_slt, is_sra, is_srl, is_sub, is_xor, not_1_out,
       not_2_out, not_3_out, or_1_out, or_3_out, or_6_out, or_8_out;
  wire [2:0] or_20_out;
  wire [4:0] or_4_out;

  Comparator #(.width(7)) comparator_1 (.a(inst[6:0]), .b(7'b0000011), .eq(comparator_1_eq));  // open: gt, lt
  Comparator #(.width(7)) comparator_2 (.a(inst[6:0]), .b(7'b0010011), .eq(comparator_2_eq));  // open: gt, lt
  Comparator #(.width(7)) comparator_3 (.a(inst[6:0]), .b(7'b0100011), .eq(or_4_out[1]));  // open: gt, lt
  Comparator #(.width(7)) comparator_4 (.a(inst[6:0]), .b(7'b1100011), .eq(or_4_out[2]));  // open: gt, lt
  Comparator #(.width(7)) comparator_5 (.a(inst[6:0]), .b(7'b0010111), .eq(comparator_5_eq));  // open: gt, lt
  Comparator #(.width(7)) comparator_6 (.a(inst[6:0]), .b(7'b0110111), .eq(comparator_6_eq));  // open: gt, lt
  Comparator #(.width(7)) comparator_7 (.a(inst[6:0]), .b(7'b1101111), .eq(or_4_out[4]));  // open: gt, lt
  Comparator #(.width(7)) comparator_8 (.a(inst[6:0]), .b(7'b1100111), .eq(comparator_8_eq));  // open: gt, lt
  Comparator #(.width(7)) comparator_9 (.a(inst[6:0]), .b(7'b1110011), .eq(comparator_9_eq));  // open: gt, lt
  or or_1 (or_1_out, comparator_1_eq, comparator_2_eq);
  or or_2 (or_4_out[3], comparator_5_eq, comparator_6_eq);
  or or_3 (or_3_out, comparator_8_eq, comparator_9_eq);
  or or_4 (or_4_out[0], or_1_out, or_3_out);
  Comparator #(.width(7)) comparator_10 (.a(inst[6:0]), .b(7'b1100011), .eq(comparator_10_eq));  // open: gt, lt
  Comparator #(.width(3)) comparator_11 (.a(inst[14:12]), .b(3'b000), .eq(comparator_11_eq));  // open: gt, lt
  Comparator #(.width(3)) comparator_12 (.a(inst[14:12]), .b(3'b001), .eq(comparator_12_eq));  // open: gt, lt
  Comparator #(.width(3)) comparator_13 (.a(inst[14:12]), .b(3'b100), .eq(comparator_13_eq));  // open: gt, lt
  Comparator #(.width(3)) comparator_14 (.a(inst[14:12]), .b(3'b101), .eq(comparator_14_eq));  // open: gt, lt
  Comparator #(.width(3)) comparator_15 (.a(inst[14:12]), .b(3'b110), .eq(comparator_15_eq));  // open: gt, lt
  Comparator #(.width(3)) comparator_16 (.a(inst[14:12]), .b(3'b111), .eq(comparator_16_eq));  // open: gt, lt
  Comparator #(.width(7)) comparator_17 (.a(inst[6:0]), .b(7'b1101111), .eq(comparator_17_eq));  // open: gt, lt
  Comparator #(.width(7)) comparator_18 (.a(inst[6:0]), .b(7'b1100111), .eq(comparator_18_eq));  // open: gt, lt
  Comparator #(.width(3)) comparator_19 (.a(inst[14:12]), .b(3'b000), .eq(comparator_19_eq));  // open: gt, lt
  Comparator #(.width(7)) comparator_20 (.a(inst[6:0]), .b(7'b1100011), .eq(comparator_20_eq));  // open: gt, lt
  Comparator #(.width(7)) comparator_21 (.a(inst[6:0]), .b(7'b1101111), .eq(comparator_21_eq));  // open: gt, lt
  Comparator #(.width(7)) comparator_22 (.a(inst[6:0]), .b(7'b0010111), .eq(comparator_22_eq));  // open: gt, lt
  Comparator #(.width(7)) comparator_23 (.a(inst[6:0]), .b(7'b0110111), .eq(comparator_23_eq));  // open: gt, lt
  and and_1 (and_1_out, comparator_18_eq, comparator_19_eq);
  Comparator #(.width(7)) comparator_24 (.a(inst[6:0]), .b(7'b0110011), .eq(comparator_24_eq));  // open: gt, lt
  Comparator #(.width(3)) comparator_25 (.a(inst[14:12]), .b(3'b000), .eq(comparator_25_eq));  // open: gt, lt
  Comparator #(.width(7)) comparator_26 (.a(inst[31:25]), .b({7{1'b0}}), .eq(comparator_26_eq));  // open: gt, lt
  Comparator #(.width(7)) comparator_27 (.a(inst[31:25]), .b(7'b0000001), .eq(comparator_27_eq));  // open: gt, lt
  Comparator #(.width(7)) comparator_28 (.a(inst[31:25]), .b(7'b0100000), .eq(comparator_28_eq));  // open: gt, lt
  Comparator #(.width(3)) comparator_29 (.a(inst[14:12]), .b(3'b001), .eq(comparator_29_eq));  // open: gt, lt
  Comparator #(.width(7)) comparator_30 (.a(inst[31:25]), .b({7{1'b0}}), .eq(comparator_30_eq));  // open: gt, lt
  Comparator #(.width(7)) comparator_31 (.a(inst[31:25]), .b(7'b0000001), .eq(comparator_31_eq));  // open: gt, lt
  Comparator #(.width(3)) comparator_32 (.a(inst[14:12]), .b(3'b011), .eq(comparator_32_eq));  // open: gt, lt
  Comparator #(.width(7)) comparator_33 (.a(inst[31:25]), .b(7'b0000001), .eq(comparator_33_eq));  // open: gt, lt
  Comparator #(.width(3)) comparator_34 (.a(inst[14:12]), .b(3'b010), .eq(comparator_34_eq));  // open: gt, lt
  Comparator #(.width(7)) comparator_35 (.a(inst[31:25]), .b({7{1'b0}}), .eq(comparator_35_eq));  // open: gt, lt
  Comparator #(.width(3)) comparator_36 (.a(inst[14:12]), .b(3'b100), .eq(comparator_36_eq));  // open: gt, lt
  Comparator #(.width(7)) comparator_37 (.a(inst[31:25]), .b({7{1'b0}}), .eq(comparator_37_eq));  // open: gt, lt
  Comparator #(.width(3)) comparator_38 (.a(inst[14:12]), .b(3'b101), .eq(comparator_38_eq));  // open: gt, lt
  Comparator #(.width(7)) comparator_39 (.a(inst[31:25]), .b({7{1'b0}}), .eq(comparator_39_eq));  // open: gt, lt
  Comparator #(.width(7)) comparator_40 (.a(inst[31:25]), .b(7'b0100000), .eq(comparator_40_eq));  // open: gt, lt
  Comparator #(.width(3)) comparator_41 (.a(inst[14:12]), .b(3'b110), .eq(comparator_41_eq));  // open: gt, lt
  Comparator #(.width(7)) comparator_42 (.a(inst[31:25]), .b({7{1'b0}}), .eq(comparator_42_eq));  // open: gt, lt
  Comparator #(.width(3)) comparator_43 (.a(inst[14:12]), .b(3'b111), .eq(comparator_43_eq));  // open: gt, lt
  Comparator #(.width(7)) comparator_44 (.a(inst[31:25]), .b({7{1'b0}}), .eq(comparator_44_eq));  // open: gt, lt
  Multiplexer #(.enable("false"), .select(5), .width(3)) multiplexer_1 (
    .in1(3'b001), .in2(3'b010), .in4(3'b011), .in8(3'b100), .in16(3'b101), .out(ImmSel), .sel(or_4_out));  // open: in0, in3, in5, in6, in7, in9, in10, in11, in12, in13, in14, in15, in17, in18, in19, in20, in21, in22, in23, in24, in25, in26, in27, in28, in29, in30, in31
  and and_2 (and_2_out, comparator_10_eq, comparator_11_eq);
  and and_3 (and_3_out, comparator_10_eq, comparator_12_eq);
  and and_4 (and_4_out, comparator_10_eq, comparator_13_eq);
  and and_5 (and_5_out, comparator_10_eq, comparator_14_eq);
  and and_6 (and_6_out, comparator_10_eq, comparator_15_eq);
  and and_7 (and_7_out, comparator_10_eq, comparator_16_eq);
  or or_5 (ASel, comparator_20_eq, comparator_21_eq, comparator_22_eq, comparator_23_eq, 1'b0);
  not not_1 (not_1_out, BrEq);
  not not_2 (not_2_out, BrLt);
  not not_3 (not_3_out, BrLt);
  and and_8 (and_8_out, comparator_24_eq, comparator_25_eq, comparator_26_eq);
  and and_9 (is_mul, comparator_24_eq, comparator_25_eq, comparator_27_eq);
  and and_10 (is_sub, comparator_24_eq, comparator_25_eq, comparator_28_eq);
  and and_11 (and_11_out, comparator_24_eq, comparator_29_eq, comparator_30_eq);
  and and_12 (is_mulh, comparator_24_eq, comparator_29_eq, comparator_31_eq);
  and and_13 (is_mulhu, comparator_24_eq, comparator_32_eq, comparator_33_eq);
  and and_14 (and_14_out, comparator_24_eq, comparator_34_eq, comparator_35_eq);
  and and_15 (and_15_out, comparator_24_eq, comparator_36_eq, comparator_37_eq);
  and and_16 (and_16_out, comparator_24_eq, comparator_38_eq, comparator_39_eq);
  and and_17 (and_17_out, comparator_24_eq, comparator_38_eq, comparator_40_eq);
  and and_18 (and_18_out, comparator_24_eq, comparator_41_eq, comparator_42_eq);
  and and_19 (and_19_out, comparator_24_eq, comparator_43_eq, comparator_44_eq);
  and and_20 (and_20_out, and_2_out, BrEq);
  and and_21 (and_21_out, and_3_out, not_1_out);
  and and_22 (and_22_out, and_4_out, BrLt);
  and and_23 (and_23_out, and_5_out, not_2_out);
  and and_24 (and_24_out, and_6_out, BrLt);
  and and_25 (and_25_out, and_7_out, not_3_out);
  or or_6 (or_6_out, comparator_17_eq, and_1_out);
  or or_7 (PCSel, 1'b0, and_20_out, and_21_out, and_22_out, and_23_out, and_24_out, and_25_out, or_6_out);
  Comparator #(.width(7)) comparator_45 (.a(inst[6:0]), .b(7'b0110011), .eq(comparator_45_eq));  // open: gt, lt
  Comparator #(.width(7)) comparator_46 (.a(inst[6:0]), .b(7'b1110011), .eq(comparator_46_eq));  // open: gt, lt
  Comparator #(.width(7)) comparator_47 (.a(inst[6:0]), .b(7'b0110011), .eq(comparator_47_eq));  // open: gt, lt
  Comparator #(.width(7)) comparator_48 (.a(inst[6:0]), .b(7'b0000011), .eq(comparator_48_eq));  // open: gt, lt
  Comparator #(.width(7)) comparator_49 (.a(inst[6:0]), .b(7'b0010011), .eq(comparator_49_eq));  // open: gt, lt
  Comparator #(.width(7)) comparator_50 (.a(inst[6:0]), .b(7'b0100011), .eq(comparator_50_eq));  // open: gt, lt
  Comparator #(.width(7)) comparator_51 (.a(inst[6:0]), .b(7'b1100011), .eq(comparator_51_eq));  // open: gt, lt
  Comparator #(.width(7)) comparator_52 (.a(inst[6:0]), .b(7'b0010111), .eq(comparator_52_eq));  // open: gt, lt
  Comparator #(.width(7)) comparator_53 (.a(inst[6:0]), .b(7'b0110111), .eq(comparator_53_eq));  // open: gt, lt
  Comparator #(.width(7)) comparator_54 (.a(inst[6:0]), .b(7'b1101111), .eq(comparator_54_eq));  // open: gt, lt
  Comparator #(.width(7)) comparator_55 (.a(inst[6:0]), .b(7'b1100111), .eq(comparator_55_eq));  // open: gt, lt
  Comparator #(.width(7)) comparator_56 (.a(inst[6:0]), .b(7'b0100011), .eq(comparator_56_eq));  // open: gt, lt
  Comparator #(.width(7)) comparator_57 (.a(inst[6:0]), .b(7'b1100011), .eq(comparator_57_eq));  // open: gt, lt
  Comparator #(.width(3)) comparator_58 (.a(inst[14:12]), .b(3'b110), .eq(comparator_58_eq));  // open: gt, lt
  Comparator #(.width(3)) comparator_59 (.a(inst[14:12]), .b(3'b111), .eq(comparator_59_eq));  // open: gt, lt
  Multiplexer #(.enable("false")) multiplexer_2 (.in0(1'b1), .in1(1'b0), .out(BSel), .sel(comparator_45_eq));
  Comparator #(.width(7)) comparator_60 (.a(inst[6:0]), .b(7'b0000011), .eq(comparator_60_eq));  // open: gt, lt
  Comparator #(.width(3)) comparator_61 (.a(inst[14:12]), .b(3'b000), .eq(comparator_61_eq));  // open: gt, lt
  Comparator #(.width(7)) comparator_62 (.a(inst[6:0]), .b(7'b0000011), .eq(comparator_62_eq));  // open: gt, lt
  Comparator #(.width(3)) comparator_63 (.a(inst[14:12]), .b(3'b001), .eq(comparator_63_eq));  // open: gt, lt
  Comparator #(.width(7)) comparator_64 (.a(inst[6:0]), .b(7'b0000011), .eq(comparator_64_eq));  // open: gt, lt
  Comparator #(.width(3)) comparator_65 (.a(inst[14:12]), .b(3'b010), .eq(comparator_65_eq));  // open: gt, lt
  Comparator #(.width(7)) comparator_66 (.a(inst[6:0]), .b(7'b0010011), .eq(comparator_66_eq));  // open: gt, lt
  Comparator #(.width(3)) comparator_67 (.a(inst[14:12]), .b(3'b000), .eq(comparator_67_eq));  // open: gt, lt
  Comparator #(.width(7)) comparator_68 (.a(inst[6:0]), .b(7'b0010011), .eq(comparator_68_eq));  // open: gt, lt
  Comparator #(.width(3)) comparator_69 (.a(inst[14:12]), .b(3'b001), .eq(comparator_69_eq));  // open: gt, lt
  Comparator #(.width(7)) comparator_70 (.a(inst[31:25]), .b({7{1'b0}}), .eq(comparator_70_eq));  // open: gt, lt
  Comparator #(.width(7)) comparator_71 (.a(inst[6:0]), .b(7'b0010011), .eq(comparator_71_eq));  // open: gt, lt
  Comparator #(.width(3)) comparator_72 (.a(inst[14:12]), .b(3'b010), .eq(comparator_72_eq));  // open: gt, lt
  Comparator #(.width(7)) comparator_73 (.a(inst[6:0]), .b(7'b0010011), .eq(comparator_73_eq));  // open: gt, lt
  Comparator #(.width(3)) comparator_74 (.a(inst[14:12]), .b(3'b100), .eq(comparator_74_eq));  // open: gt, lt
  Comparator #(.width(7)) comparator_75 (.a(inst[6:0]), .b(7'b0010011), .eq(comparator_75_eq));  // open: gt, lt
  Comparator #(.width(3)) comparator_76 (.a(inst[14:12]), .b(3'b101), .eq(comparator_76_eq));  // open: gt, lt
  Comparator #(.width(7)) comparator_77 (.a(inst[31:25]), .b({7{1'b0}}), .eq(comparator_77_eq));  // open: gt, lt
  Comparator #(.width(7)) comparator_78 (.a(inst[6:0]), .b(7'b0010011), .eq(comparator_78_eq));  // open: gt, lt
  Comparator #(.width(3)) comparator_79 (.a(inst[14:12]), .b(3'b101), .eq(comparator_79_eq));  // open: gt, lt
  Comparator #(.width(7)) comparator_80 (.a(inst[31:25]), .b(7'b0100000), .eq(comparator_80_eq));  // open: gt, lt
  Comparator #(.width(7)) comparator_81 (.a(inst[6:0]), .b(7'b0010011), .eq(comparator_81_eq));  // open: gt, lt
  Comparator #(.width(3)) comparator_82 (.a(inst[14:12]), .b(3'b110), .eq(comparator_82_eq));  // open: gt, lt
  Comparator #(.width(7)) comparator_83 (.a(inst[6:0]), .b(7'b0010011), .eq(comparator_83_eq));  // open: gt, lt
  Comparator #(.width(3)) comparator_84 (.a(inst[14:12]), .b(3'b111), .eq(comparator_84_eq));  // open: gt, lt
  and and_26 (and_26_out, comparator_46_eq, 1'b1);
  and and_27 (and_27_out, comparator_47_eq, 1'b1);
  and and_28 (and_28_out, comparator_48_eq, 1'b1);
  and and_29 (and_29_out, comparator_49_eq, 1'b1);
  and and_30 (and_30_out, comparator_50_eq, 1'b0);
  and and_31 (and_31_out, comparator_51_eq, 1'b0);
  and and_32 (and_32_out, comparator_52_eq, 1'b1);
  and and_33 (and_33_out, comparator_53_eq, 1'b1);
  and and_34 (and_34_out, comparator_54_eq, 1'b1);
  and and_35 (and_35_out, comparator_55_eq, 1'b1);
  and and_36 (MemRW, comparator_56_eq, 1'b1);
  or or_8 (or_8_out, comparator_58_eq, comparator_59_eq);
  and and_37 (and_37_out, comparator_60_eq, comparator_61_eq);
  and and_38 (and_38_out, comparator_62_eq, comparator_63_eq);
  and and_39 (and_39_out, comparator_64_eq, comparator_65_eq);
  and and_40 (and_40_out, comparator_66_eq, comparator_67_eq);
  and and_41 (and_41_out, comparator_68_eq, comparator_69_eq, comparator_70_eq);
  and and_42 (and_42_out, comparator_71_eq, comparator_72_eq);
  and and_43 (and_43_out, comparator_73_eq, comparator_74_eq);
  and and_44 (and_44_out, comparator_75_eq, comparator_76_eq, comparator_77_eq);
  and and_45 (and_45_out, comparator_78_eq, comparator_79_eq, comparator_80_eq);
  and and_46 (and_46_out, comparator_81_eq, comparator_82_eq);
  and and_47 (and_47_out, comparator_83_eq, comparator_84_eq);
  and and_48 (and_48_out, comparator_57_eq, or_8_out);
  or or_9 (RegWEn, and_26_out, and_27_out, and_28_out, and_29_out, and_30_out, 1'b0, and_31_out, and_32_out, and_33_out, and_34_out, and_35_out);
  or or_10 (BrUn, and_48_out, 1'b0);
  or or_11 (is_sll, and_41_out, and_11_out);
  or or_12 (is_slt, and_42_out, and_14_out);
  or or_13 (is_xor, and_43_out, and_15_out);
  or or_14 (is_srl, and_44_out, and_16_out);
  or or_15 (is_sra, and_45_out, and_17_out);
  or or_16 (is_or, and_46_out, and_18_out);
  or or_17 (is_and, and_47_out, and_19_out);
  Comparator #(.width(7)) comparator_85 (.a(inst[6:0]), .b(7'b1110011), .eq(comparator_85_eq));  // open: gt, lt
  Comparator #(.width(7)) comparator_86 (.a(inst[6:0]), .b(7'b0100011), .eq(comparator_86_eq));  // open: gt, lt
  Comparator #(.width(7)) comparator_87 (.a(inst[6:0]), .b(7'b1100011), .eq(comparator_87_eq));  // open: gt, lt
  Comparator #(.width(7)) comparator_88 (.a(inst[6:0]), .b(7'b0010111), .eq(comparator_88_eq));  // open: gt, lt
  Comparator #(.width(7)) comparator_89 (.a(inst[6:0]), .b(7'b0110111), .eq(comparator_89_eq));  // open: gt, lt
  Comparator #(.width(7)) comparator_90 (.a(inst[6:0]), .b(7'b1101111), .eq(comparator_90_eq));  // open: gt, lt
  Comparator #(.width(7)) comparator_91 (.a(inst[6:0]), .b(7'b1100111), .eq(comparator_91_eq));  // open: gt, lt
  Comparator #(.width(7)) comparator_92 (.a(inst[6:0]), .b(7'b1110011), .eq(comparator_92_eq));  // open: gt, lt
  Comparator #(.width(7)) comparator_93 (.a(inst[6:0]), .b(7'b0000011), .eq(comparator_93_eq));  // open: gt, lt
  Comparator #(.width(3)) comparator_94 (.a(inst[14:12]), .b(3'b000), .eq(comparator_94_eq));  // open: gt, lt
  Comparator #(.width(3)) comparator_95 (.a(inst[14:12]), .b(3'b001), .eq(comparator_95_eq));  // open: gt, lt
  Comparator #(.width(3)) comparator_96 (.a(inst[14:12]), .b(3'b010), .eq(comparator_96_eq));  // open: gt, lt
  Comparator #(.width(7)) comparator_97 (.a(inst[6:0]), .b(7'b0110011), .eq(comparator_97_eq));  // open: gt, lt
  Comparator #(.width(7)) comparator_98 (.a(inst[6:0]), .b(7'b0010011), .eq(comparator_98_eq));  // open: gt, lt
  Comparator #(.width(7)) comparator_99 (.a(inst[6:0]), .b(7'b0010111), .eq(comparator_99_eq));  // open: gt, lt
  Comparator #(.width(7)) comparator_100 (.a(inst[6:0]), .b(7'b0110111), .eq(comparator_100_eq));  // open: gt, lt
  Comparator #(.width(7)) comparator_101 (.a(inst[6:0]), .b(7'b1101111), .eq(comparator_101_eq));  // open: gt, lt
  Comparator #(.width(7)) comparator_102 (.a(inst[6:0]), .b(7'b1100111), .eq(comparator_102_eq));  // open: gt, lt
  Comparator #(.width(7)) comparator_103 (.a(inst[6:0]), .b(7'b1110011), .eq(comparator_103_eq));  // open: gt, lt
  Comparator #(.width(3)) comparator_104 (.a(inst[14:12]), .b(3'b101), .eq(comparator_104_eq));  // open: gt, lt
  Comparator #(.width(7)) comparator_105 (.a(inst[6:0]), .b(7'b1110011), .eq(CSRWen));  // open: gt, lt
  and and_49 (CSRSel, comparator_103_eq, comparator_104_eq);
  or or_18 (is_add, and_8_out, and_37_out, and_38_out, and_39_out, and_40_out, comparator_87_eq, comparator_88_eq, comparator_90_eq, comparator_91_eq, comparator_86_eq);
  or or_19 (is_bsel, comparator_89_eq, comparator_92_eq);
  and and_50 (and_50_out, comparator_93_eq, comparator_94_eq);
  and and_51 (and_51_out, comparator_93_eq, comparator_95_eq);
  and and_52 (and_52_out, comparator_93_eq, comparator_96_eq);
  or or_20 (or_20_out[0], and_50_out, and_51_out, and_52_out);
  or or_21 (or_20_out[1], comparator_97_eq, comparator_98_eq, comparator_85_eq, comparator_99_eq, comparator_100_eq);
  or or_22 (or_20_out[2], comparator_101_eq, comparator_102_eq);
  Priority_Encoder #(.select(4)) priority_encoder_1 (
    .in0(is_add), .in1(is_sll), .in2(is_slt), .in4(is_xor), .in5(is_srl), .in6(is_or), .in7(is_and),
    .in8(is_mul), .in9(is_mulh), .in11(is_mulhu), .in12(is_sub), .in13(is_sra), .in15(is_bsel), .out(ALUSel));  // open: in3, in10, in14, gs, en_out, en_in
  Multiplexer #(.enable("false"), .select(3), .width(2)) multiplexer_3 (
    .in1(2'b10), .in2(2'b01), .in4(2'b00), .out(WBSel), .sel(or_20_out));  // open: in0, in3, in5, in6, in7

  // Other names for the same wires on the sheet: opcode[6:0] = inst[6:0]; rd[4:0] = inst[11:7];
  //   func3[2:0] = inst[14:12]; rs1[4:0] = inst[19:15]; rs2[4:0] = inst[24:20]; func7[6:0] = inst[31:25]

  // Notes on the sheet:
  //   INPUTS to your circuit
  //   beq
  //   bne
  //   blt
  //   bge
  //   bltu
  //   bgeu
  //   jal
  //   jalr
  //   add
  //   mul
  //   sub
  //   sll
  //   mulh
  //   mulhu
  //   slt
  //   xor
  //   srl
  //   sra
  //   or
  //   and
  //   DON'T CHANGE THE LOCATIONS OF THE INPUTS AND OUTPUTS!
  //   OUTPUT from your circuit
  //   PCSel
  //   ASel
  //   R Type
  //   lb
  //   lh
  //   lw
  //   addi
  //   slli
  //   slti
  //   xori
  //   srli
  //   srai
  //   ori
  //   andi
  //   BSel
  //   I Type
  //   ALUSel
  //   S Type
  //   other I Type
  //   SB Type
  //   U Type
  //   UJ Type
  //   WBSel mem
  //   WBSel ALU
  //   WBSel PC+4
endmodule
