// Logisim project cpu.circ as structural Verilog: 1 circuit, main circuit cpu
module cpu (
  input  clk,
  input  [31:0] INSTRUCTION,
  input  [31:0] READ_DATA,
  output [31:0] WRITE_ADDRESS,
  output [31:0] PROGRAM_COUNTER,
  output [31:0] ra,
  output [31:0] sp,
  output [31:0] t0,
  output [31:0] t1,
  output [31:0] t2,
  output [31:0] s0,
  output [31:0] s1,
  output [31:0] a0,
  output [31:0] tohost,
  output [3:0] WRITE_ENABLE,
  output [31:0] WRITE_DATA
);

  wire ASel, BrEq, BrLt, BrUn, BSel, CSRSel, CSRWen, MemRw, PCSel, RegWEn;
  wire [1:0] WBSel;
  wire [2:0] func3, ImmSel;
  wire [3:0] ALUSel, multiplexer_6_out, shifter_2_out;
  wire [4:0] bit_extender_4_out, bit_shift;
  wire [6:0] opcode;
  wire [7:0] shifter_1_out;
  wire [11:0] CSR_address;
  wire [15:8] shifter_1_out_2;
  wire [19:7] p_INSTRUCTION;
  wire [31:0] adder_2_out, bit_extender_1_out, bit_extender_2_out, bit_extender_3_out, imm, input_A, input_B,
       multiplexer_2_out, multiplexer_3_out, out_data, p_pc, PC4, PC_input, result1, result2, Write_Data_t;
  wire [31:16] shifter_1_out_3;

  Multiplexer #(.enable("false"), .width(32)) multiplexer_1 (
    .in0(PC4), .in1(WRITE_ADDRESS), .out(PC_input), .sel(PCSel));
  assign bit_extender_1_out = {{27{1'b0}}, p_INSTRUCTION[19:15]};  // Bit_Extender bit_extender_1
  Adder #(.width(32)) adder_1 (.a(PROGRAM_COUNTER), .b(32'h4), .out(PC4));  // open: cin, cout
  Register #(.width(32)) PC (.D(PC_input), .clk(clk), .Q(PROGRAM_COUNTER));  // open: en, clr
  Multiplexer #(.enable("false"), .width(32)) multiplexer_2 (
    .in0(result1), .in1(bit_extender_1_out), .out(multiplexer_2_out), .sel(CSRSel));
  Multiplexer #(.enable("false"), .width(32)) multiplexer_3 (
    .in0(INSTRUCTION), .in1(32'h13), .out(multiplexer_3_out), .sel(PCSel));
  Register #(.width(32)) register_1 (.D(PROGRAM_COUNTER), .clk(clk), .Q(p_pc));  // open: en, clr
  Register #(.width(32)) register_2 (
    .D(multiplexer_3_out), .clk(clk),
    .Q({CSR_address, p_INSTRUCTION[19:15], func3, p_INSTRUCTION[11:7], opcode}));  // open: en, clr
  imm_gen imm_gen_1 (
    .inst({CSR_address, p_INSTRUCTION[19:15], func3, p_INSTRUCTION[11:7], opcode}), .ImmSel(ImmSel), .imm(imm));
  // csr csr_1: pin names not known; wires that end beside it: multiplexer_2_out, CSRWen, clk, CSR_address, tohost
  control_logic control_logic_1 (
    .CSRWen(CSRWen), .PCSel(PCSel), .RegWEn(RegWEn), .ImmSel(ImmSel), .BrUn(BrUn), .ASel(ASel), .BSel(BSel),
    .ALUSel(ALUSel), .MemRW(MemRw), .WBSel(WBSel), .CSRSel(CSRSel),
    .inst({CSR_address, p_INSTRUCTION[19:15], func3, p_INSTRUCTION[11:7], opcode}), .BrEq(BrEq), .BrLt(BrLt));
  regfile regfile_1 (
    .rs1(p_INSTRUCTION[19:15]), .rs2(CSR_address[4:0]), .rd(p_INSTRUCTION[11:7]), .Write_Data(Write_Data_t),
    .RegWEn(RegWEn), .clk(clk), .ra(ra), .sp(sp), .t0(t0), .t1(t1), .t2(t2), .s0(s0), .s1(s1), .a0(a0),
    .Read_Data_1(result1), .Read_Data_2(result2));
  Multiplexer #(.enable("false"), .width(32)) multiplexer_4 (.in0(result1), .in1(p_pc), .out(input_A), .sel(ASel));
  Multiplexer #(.enable("false"), .width(32)) multiplexer_5 (.in0(result2), .in1(imm), .out(input_B), .sel(BSel));
  branch_comp branch_comp_1 (.rs1(result1), .rs2(result2), .BrUn(BrUn), .BrEq(BrEq), .BrLt(BrLt));
  alu alu_1 (.Result(WRITE_ADDRESS), .A(input_A), .B(input_B), .ALUSel(ALUSel));
  Multiplexer #(.enable("false"), .select(2), .width(4)) multiplexer_6 (
    .in0(4'b0001), .in1(4'b0011), .in2(4'b1111), .out(multiplexer_6_out), .sel(func3[1:0]));  // open: in3
  Shifter #(.shift("lr"), .width(32)) shifter_1 (
    .in(READ_DATA), .\dist (bit_shift), .out({shifter_1_out_3, shifter_1_out_2, shifter_1_out}));
  Shifter #(.width(4)) shifter_2 (.in(multiplexer_6_out), .\dist (WRITE_ADDRESS[1:0]), .out(shifter_2_out));
  Shifter #(.width(32)) shifter_3 (.in(result2), .\dist (bit_shift), .out(WRITE_DATA));
  assign bit_extender_2_out = {{24{shifter_1_out[7]}}, shifter_1_out};  // Bit_Extender bit_extender_2
  assign bit_extender_3_out = {{16{shifter_1_out_2[15]}}, {shifter_1_out_2, shifter_1_out}};  // Bit_Extender bit_extender_3
  assign bit_extender_4_out = {{3{WRITE_ADDRESS[1]}}, WRITE_ADDRESS[1:0]};  // Bit_Extender bit_extender_4
  Multiplexer #(.enable("false"), .width(4)) multiplexer_7 (
    .in0(4'b0000), .in1(shifter_2_out), .out(WRITE_ENABLE), .sel(MemRw));
  Multiplexer #(.enable("false"), .select(2), .width(32)) multiplexer_8 (
    .in0(bit_extender_2_out), .in1(bit_extender_3_out),
    .in2({shifter_1_out_3, shifter_1_out_2, shifter_1_out}), .out(out_data), .sel(func3[1:0]));  // open: in3
  Adder #(.width(32)) adder_2 (.a(p_pc), .b(32'h4), .out(adder_2_out));  // open: cin, cout
  Multiplier #(.width(5)) multiplier_1 (.a(bit_extender_4_out), .b(5'b01000), .out(bit_shift));  // open: cin, cout
  Multiplexer #(.enable("false"), .select(2), .width(32)) multiplexer_9 (
    .in0(adder_2_out), .in1(WRITE_ADDRESS), .in2(out_data), .out(Write_Data_t), .sel(WBSel));  // open: in3

  // Other names for the same wires on the sheet: p_INSTRUCTION (some bits) = {CSR_address, func3, opcode};
  //   rd[4:0] = p_INSTRUCTION[11:7]; rs1[4:0] = p_INSTRUCTION[19:15]; rs2[4:0] = CSR_address[4:0];
  //   func7[6:0] = CSR_address[11:5]; result_output[31:0] = WRITE_ADDRESS

  // Notes on the sheet:
  //   Output to IMEM
  //   IMEM (do **NOT** move this)
  //   Inputs from IMEM
  //   It is OK to move the PC, RegFile, ALU, MEM, Branch Comp, Imm Gen, and Control Logic to wherever is most convenient for you when constructing your CPU, and to delete this text
  //   Inputs/Outputs for testing. Do **NOT** move these.
  //   Outputs To DMEM
  //   DMEM (do **NOT** move this)
  //   Inputs From DMEM
endmodule
