// Logisim project imm-gen.circ as structural Verilog: 1 circuit, main circuit imm_gen
module imm_gen (
  input  [31:0] inst,
  input  [2:0] ImmSel,
  output [31:0] imm
);

  wire [31:0] R;
  wire [31:11] I, S;
  wire [31:12] SB;
  wire [31:20] UJ;

  Multiplexer #(.enable("false"), .width(21)) multiplexer_1 (
    .in0({21{1'b0}}), .in1({21{1'b1}}), .out(I), .sel(inst[31]));
  Multiplexer #(.enable("false"), .width(21)) multiplexer_2 (
    .in0({21{1'b0}}), .in1({21{1'b1}}), .out(S), .sel(inst[31]));
  Multiplexer #(.enable("false"), .width(20)) multiplexer_3 (
    .in0({20{1'b0}}), .in1({20{1'b1}}), .out(SB), .sel(inst[31]));
  Multiplexer #(.enable("false"), .width(12)) multiplexer_4 (
    .in0({12{1'b0}}), .in1({12{1'b1}}), .out(UJ), .sel(inst[31]));
  Multiplexer #(.enable("false"), .select(3), .width(32)) multiplexer_5 (
    .in0(R), .in1({I, inst[30:20]}), .in2({S, inst[30:25], inst[11:7]}),
    .in3({SB, inst[7], inst[30:25], inst[11:8], 1'b0}), .in4({inst[31:12], {12{1'b0}}}),
    .in5({UJ, inst[19:12], inst[20], inst[30:21], 1'b0}), .out(imm), .sel(ImmSel));  // open: in6, in7

  // Other names for the same wires on the sheet: S[10:0] = {inst[30:25], inst[11:7]};
  //   SB[11:1] = {inst[7], inst[30:25], inst[11:8]}; U[31:12] = inst[31:12]; I[10:0] = inst[30:20];
  //   UJ[19:1] = {inst[19:12], inst[20], inst[30:21]}

  // Notes on the sheet:
  //   INPUTS to your circuit
  //   DON'T CHANGE THE LOCATIONS OF THE INPUTS AND OUTPUTS!
  //   OUTPUT from your circuit
endmodule
