// Logisim project regfile.circ as structural Verilog: 1 circuit, main circuit regfile
module regfile (
  input  [4:0] rs1,
  input  [4:0] rs2,
  input  [4:0] rd,
  input  [31:0] Write_Data,
  input  RegWEn,
  input  clk,
  output [31:0] ra,
  output [31:0] sp,
  output [31:0] t0,
  output [31:0] t1,
  output [31:0] t2,
  output [31:0] s0,
  output [31:0] s1,
  output [31:0] a0,
  output [31:0] Read_Data_1,
  output [31:0] Read_Data_2
);

  wire wa0, wa1, wa2, wa3, wa4, wa5, wa6, wa7, wgp, wra, ws0, ws1, ws2, ws3, ws4, ws5, ws6, ws7, ws8, ws9,
       ws10, ws11, wsp, wt0, wt1, wt2, wt3, wt4, wt5, wt6, wtp;
  wire [31:0] a1, a2, a3, a4, a5, a6, a7, gp, s2, s3, s4, s5, s6, s7, s8, s9, s10, s11, t3, t4, t5, t6, tp,
       x0;

  Register #(.width(32)) register_1 (.D(Write_Data), .en(wra), .clk(clk), .Q(ra));  // open: clr
  Register #(.width(32)) register_2 (.D(Write_Data), .en(wsp), .clk(clk), .Q(sp));  // open: clr
  Register #(.width(32)) register_3 (.D(Write_Data), .en(wt0), .clk(clk), .Q(t0));  // open: clr
  Register #(.width(32)) register_4 (.D(Write_Data), .en(wt1), .clk(clk), .Q(t1));  // open: clr
  Multiplexer #(.enable("false"), .select(5), .width(32)) multiplexer_1 (
    .in0(x0), .in1(ra), .in2(sp), .in3(gp), .in4(tp), .in5(t0), .in6(t1), .in7(t2), .in8(s0), .in9(s1),
    .in10(a0), .in11(a1), .in12(a2), .in13(a3), .in14(a4), .in15(a5), .in16(a6), .in17(a7), .in18(s2),
    .in19(s3), .in20(s4), .in21(s5), .in22(s6), .in23(s7), .in24(s8), .in25(s9), .in26(s10), .in27(s11),
    .in28(t3), .in29(t4), .in30(t5), .in31(t6), .out(Read_Data_1), .sel(rs1));
  Register #(.width(32)) register_5 (.D(Write_Data), .en(ws3), .clk(clk), .Q(s3));  // open: clr
  Register #(.width(32)) register_6 (.D(Write_Data), .en(ws4), .clk(clk), .Q(s4));  // open: clr
  Register #(.width(32)) register_7 (.D(Write_Data), .en(ws5), .clk(clk), .Q(s5));  // open: clr
  Register #(.width(32)) register_8 (.D(Write_Data), .en(ws6), .clk(clk), .Q(s6));  // open: clr
  Register #(.width(32)) register_9 (.D(Write_Data), .en(wt2), .clk(clk), .Q(t2));  // open: clr
  Register #(.width(32)) register_10 (.D(Write_Data), .en(ws0), .clk(clk), .Q(s0));  // open: clr
  Register #(.width(32)) register_11 (.D(Write_Data), .en(ws1), .clk(clk), .Q(s1));  // open: clr
  Register #(.width(32)) register_12 (.D(Write_Data), .en(wa0), .clk(clk), .Q(a0));  // open: clr
  Register #(.width(32)) register_13 (.D(Write_Data), .en(ws7), .clk(clk), .Q(s7));  // open: clr
  Register #(.width(32)) register_14 (.D(Write_Data), .en(ws8), .clk(clk), .Q(s8));  // open: clr
  Register #(.width(32)) register_15 (.D(Write_Data), .en(ws9), .clk(clk), .Q(s9));  // open: clr
  Register #(.width(32)) register_16 (.D(Write_Data), .en(ws10), .clk(clk), .Q(s10));  // open: clr
  Multiplexer #(.enable("false"), .select(5), .width(32)) multiplexer_2 (
    .in0(x0), .in1(ra), .in2(sp), .in3(gp), .in4(tp), .in5(t0), .in6(t1), .in7(t2), .in8(s0), .in9(s1),
    .in10(a0), .in11(a1), .in12(a2), .in13(a3), .in14(a4), .in15(a5), .in16(a6), .in17(a7), .in18(s2),
    .in19(s3), .in20(s4), .in21(s5), .in22(s6), .in23(s7), .in24(s8), .in25(s9), .in26(s10), .in27(s11),
    .in28(t3), .in29(t4), .in30(t5), .in31(t6), .out(Read_Data_2), .sel(rs2));
  Register #(.width(32)) register_17 (.D({32{1'b0}}), .en(1'b1), .clk(clk), .Q(x0));  // open: clr
  Register #(.width(32)) register_18 (.D(Write_Data), .en(wa1), .clk(clk), .Q(a1));  // open: clr
  Register #(.width(32)) register_19 (.D(Write_Data), .en(wa2), .clk(clk), .Q(a2));  // open: clr
  Register #(.width(32)) register_20 (.D(Write_Data), .en(wa3), .clk(clk), .Q(a3));  // open: clr
  Register #(.width(32)) register_21 (.D(Write_Data), .en(wa4), .clk(clk), .Q(a4));  // open: clr
  Register #(.width(32)) register_22 (.D(Write_Data), .en(ws11), .clk(clk), .Q(s11));  // open: clr
  Register #(.width(32)) register_23 (.D(Write_Data), .en(wt3), .clk(clk), .Q(t3));  // open: clr
  Register #(.width(32)) register_24 (.D(Write_Data), .en(wt4), .clk(clk), .Q(t4));  // open: clr
  Register #(.width(32)) register_25 (.D(Write_Data), .en(wt5), .clk(clk), .Q(t5));  // open: clr
  Demultiplexer #(.enable("false"), .select(5)) demultiplexer_1 (
    .out1(wra), .out2(wsp), .out3(wgp), .out4(wtp), .out5(wt0), .out6(wt1), .out7(wt2), .out8(ws0),
    .out9(ws1), .out10(wa0), .out11(wa1), .out12(wa2), .out13(wa3), .out14(wa4), .out15(wa5), .out16(wa6),
    .out17(wa7), .out18(ws2), .out19(ws3), .out20(ws4), .out21(ws5), .out22(ws6), .out23(ws7), .out24(ws8),
    .out25(ws9), .out26(ws10), .out27(ws11), .out28(wt3), .out29(wt4), .out30(wt5), .out31(wt6), .in(RegWEn),
    .sel(rd));  // open: out0
  Register #(.width(32)) register_26 (.D(Write_Data), .en(wa5), .clk(clk), .Q(a5));  // open: clr
  Register #(.width(32)) register_27 (.D(Write_Data), .en(wa6), .clk(clk), .Q(a6));  // open: clr
  Register #(.width(32)) register_28 (.D(Write_Data), .en(wa7), .clk(clk), .Q(a7));  // open: clr
  Register #(.width(32)) register_29 (.D(Write_Data), .en(ws2), .clk(clk), .Q(s2));  // open: clr
  Register #(.width(32)) register_30 (.D(Write_Data), .en(wt6), .clk(clk), .Q(t6));  // open: clr
  Register #(.width(32)) register_31 (.D(Write_Data), .en(wgp), .clk(clk), .Q(gp));  // open: clr
  Register #(.width(32)) register_32 (.D(Write_Data), .en(wtp), .clk(clk), .Q(tp));  // open: clr

  // Other names for the same wires on the sheet: read_data1[31:0] = Read_Data_1; read_data2[31:0] = Read_Data_2;
  //   read_reg1[4:0] = rs1; read_reg2[4:0] = rs2; write_en = RegWEn; write_reg[4:0] = rd

  // Notes on the sheet:
  //   INPUTS to your circuit
  //   DON'T CHANGE THE LOCATIONS OF THE INPUTS AND OUTPUTS!
  //   These are DEBUG/TEST outputs from your circuit.
  //   OUTPUTS from your circuit
endmodule
