// Logisim project cpu-R_type.circ as structural Verilog: 1 circuit, main circuit run_main
module run_main (
  output [31:0] ra,
  output [31:0] sp,
  output [31:0] t0,
  output [31:0] t1,
  output [31:0] t2,
  output [31:0] s0,
  output [31:0] s1,
  output [31:0] a0,
  output [31:0] Requested_Address,
  output [31:0] Requested_Instruction,
  output [15:0] Time_Step,
  output halt
);

  wire clk;

  Clock clock_1 (.out(clk));
  // Probe on Requested_Address
  // cpu_harness cpu_harness_1: pin names not known; wires that end beside it: Requested_Instruction, clk, Requested_Address, ra, sp, t0, t1, t2, s0, s1, a0
  ROM #(.addrWidth(14), .dataWidth(32)) rom_1 (.addr(Requested_Address[15:2]), .data(Requested_Instruction));
  // Probe on Requested_Instruction
  Counter #(.max('hffff), .width(16)) counter_1 (.clk(clk), .Q(Time_Step));  // open: clr, load, up, count, D, carry
  Comparator #(.width(16)) comparator_1 (.a(Time_Step), .b(16'h13), .eq(halt));  // open: gt, lt

  // Other names for the same wires on the sheet: INSTRUCTION[31:0] = Requested_Instruction;
  //   PROGRAM_COUNTER[31:0] = Requested_Address

  // Notes on the sheet:
  //   contents of rom_1 (hex, n*v repeats v):
  //   100413 40433 40840433 240413 404B3 2940433 941433 945433 942433 2941433 348E13 9E4333 2933433 200E93
  //   41D45433 1D4E4B3 997933
  //   Instruction Memory
  //   Halts Execution After Constant # of Clock Cycles
  //   Constant
endmodule
