// Logisim project cpu-all_instructions.circ as structural Verilog: 1 circuit, main circuit run_main
module run_main (
  output [31:0] ra,
  output [31:0] sp,
  output [31:0] t0,
  output [31:0] t1,
  output [31:0] t2,
  output [31:0] s0,
  output [31:0] s1,
  output [31:0] a0,
  output [31:0] Requested_Address,
  output [31:0] Requested_Instruction,
  output [15:0] Time_Step,
  output halt
);

  wire clk;

  Clock clock_1 (.out(clk));
  // Probe on Requested_Address
  // cpu_harness cpu_harness_1: pin names not known; wires that end beside it: Requested_Instruction, clk, Requested_Address, ra, sp, t0, t1, t2, s0, s1, a0
  ROM #(.addrWidth(14), .dataWidth(32)) rom_1 (.addr(Requested_Address[15:2]), .data(Requested_Instruction));
  // Probe on Requested_Instruction
  Counter #(.max('hffff), .width(16)) counter_1 (.clk(clk), .Q(Time_Step));  // open: clr, load, up, count, D, carry
  Comparator #(.width(16)) comparator_1 (.a(Time_Step), .b(16'h22), .eq(halt));  // open: gt, lt

  // Other names for the same wires on the sheet: INSTRUCTION[31:0] = Requested_Instruction;
  //   PROGRAM_COUNTER[31:0] = Requested_Address

  // Notes on the sheet:
  //   contents of rom_1 (hex, n*v repeats v):
  //   33 6400593 2B00533 40058533 B59533 2B59533 2B5B533 B5A533 B5C533 B5D533 40B5D533 B5E533 5F533
  //   6450603 6451603 6452603 80058593 359513 45A513 655C513 A5D513 40A5D513 655E513 655F513 6A58223
  //   A59023 A5A123 3E9517 7E4537 64000EF 64500E7
  //   Instruction Memory
  //   Halts Execution After Constant # of Clock Cycles
  //   Constant
endmodule
