// Logisim project cpu-mem.circ as structural Verilog: 1 circuit, main circuit run_main
module run_main (
  output [31:0] ra,
  output [31:0] sp,
  output [31:0] t0,
  output [31:0] t1,
  output [31:0] t2,
  output [31:0] s0,
  output [31:0] s1,
  output [31:0] a0,
  output [31:0] Requested_Address,
  output [31:0] Requested_Instruction,
  output [15:0] Time_Step,
  output halt
);

  wire clk;

  Clock clock_1 (.out(clk));
  // Probe on Requested_Address
  // cpu_harness cpu_harness_1: pin names not known; wires that end beside it: Requested_Instruction, clk, Requested_Address, ra, sp, t0, t1, t2, s0, s1, a0
  ROM #(.addrWidth(14), .dataWidth(32)) rom_1 (.addr(Requested_Address[15:2]), .data(Requested_Instruction));
  // Probe on Requested_Instruction
  Counter #(.max('hffff), .width(16)) counter_1 (.clk(clk), .Q(Time_Step));  // open: clr, load, up, count, D, carry
  Comparator #(.width(16)) comparator_1 (.a(Time_Step), .b(16'h40), .eq(halt));  // open: gt, lt

  // Other names for the same wires on the sheet: INSTRUCTION[31:0] = Requested_Instruction;
  //   PROGRAM_COUNTER[31:0] = Requested_Address

  // Notes on the sheet:
  //   contents of rom_1 (hex, n*v repeats v):
  //   FFC10113 8AE437 8AE697 10000A93 8AA023 AA483 8A9A23 7D04B7 9AAA23 9A8AA3 29A9423 FE9A8D23 C09A8C23
  //   7D000913 E69A9823 C09AAC23 C18AA483 FF00B13 7E9B2C23 809B2423 FE9B2E23 9B0523 FE9B0DA3 9B1823 9B1923
  //   FE9B1D23 FFB00A93 15B2C23 18B0A03 AAA023 BAA023 CAA023 DAA023 EAA023 FAA023 10AA023 11AA023 8AA023
  //   9AA023 12AA023 13AA023 14AA023 16AA023 17AA023 18AA023 19AA023 1AAA023 1BAA023 5AA023 6AA023 7AA023
  //   1CAA023 1DAA023 1EAA023 1FAA023 AA283 AA303 AA383 AAE03 AAE83 AAF03 AAF83
  //   Instruction Memory
  //   Halts Execution After Constant # of Clock Cycles
  //   Constant
endmodule
