// Logisim project cpu-test_randomized.circ as structural Verilog: 1 circuit, main circuit run_main
module run_main (
  output [31:0] ra,
  output [31:0] sp,
  output [31:0] t0,
  output [31:0] t1,
  output [31:0] t2,
  output [31:0] s0,
  output [31:0] s1,
  output [31:0] a0,
  output [31:0] Requested_Address,
  output [31:0] Requested_Instruction,
  output [15:0] Time_Step,
  output halt
);

  wire clk;

  Clock clock_1 (.out(clk));
  // Probe on Requested_Address
  // cpu_harness cpu_harness_1: pin names not known; wires that end beside it: Requested_Instruction, clk, Requested_Address, ra, sp, t0, t1, t2, s0, s1, a0
  ROM #(.addrWidth(14), .dataWidth(32)) rom_1 (.addr(Requested_Address[15:2]), .data(Requested_Instruction));
  // Probe on Requested_Instruction
  Counter #(.max('hffff), .width(16)) counter_1 (.clk(clk), .Q(Time_Step));  // open: clr, load, up, count, D, carry
  Comparator #(.width(16)) comparator_1 (.a(Time_Step), .b(16'hc1d), .eq(halt));  // open: gt, lt

  // Other names for the same wires on the sheet: INSTRUCTION[31:0] = Requested_Instruction;
  //   PROGRAM_COUNTER[31:0] = Requested_Address

  // Notes on the sheet:
  //   contents of rom_1 (hex, n*v repeats v):
  //   FFFC137 80010113 10513 FFFC5B7 13 52023 450513 B50463 FE0008E3 13 C800A67 9063C513 2E488937 DF105A3
  //   321103A3 5EC00CE7 78C004E7 F6F1CE13 260008E7 37800DE7 D764B2B7 54C9D0EF 2D800C67 456C19EF 5E2F74EF
  //   5C18413 12646313 3FE9233 CE10683 19800A67 A4F3B3 204D62EF 41F43997 6A4A2EF 58E9B1EF 33C99B3 5D510803
  //   3025CBEF 5000D67 37510283 218006E7 899533 87CFB3 1419536F 58FE966F 7A4101A3 3B010523 55410003
  //   22C3E4EF 4619396F E10A6513 17F9433 54E10623 54310383 1386033 74AE1037 2421833 41000DE7 638000E7
  //   42710E03 4B0AF86F 1FC346F 64A80A6F 6BBA3EEF E010323 349FB3 143103A3 688007E7 3F031B3 8800B67
  //   1F857193 2F3E13EF 7CB50BEF 3410E83 279E7A6F 76C6FA93 AD6333 4E800067 6B010DA3 4EC00667 7AC007E7
  //   B6E67417 12000567 57B102A3 6AD4C56F 155108A3 6E800BE7 39F3D4EF 5F10923 7D800967 41710AA3 1C891B3
  //   6EE333 13C10503 6AC4466F 48C00367 5C94336F 388006E7 28910683 2B800DE7 3C001E7 5A8008E7 EF1E2293
  //   70910D23 F84E1AB7 58B10CA3 41E10F83 72E10DA3 79C00B67 4738DB6F A69533 5AE10DA3 A800B67 3127DEF
  //   460004E7 69010D83 41D90A33 70C00967 2E6100A3 1618D5EF 5C000BE7 17000BE7 680001E7 788006E7 3A09EB3
  //   17404B3 33BD2D13 BF102A3 44E6693 5503B5EF 7E910F03 3FFDA6EF 28EEA37 68310903 4AC00867 22310823
  //   6410503 6E21E693 1C36F33 9000067 6E000767 12C2B06F 63C10E23 41F28CB3 4C2EC96F 106AB6F 1A010403
  //   74D10E83 1B48333 F16E0397 406E8B33 78C002E7 40400A67 DDFFB3 6C510F23 1C4007E7 752306EF 5477486F
  //   7D5081EF 47910683 76400367 C6E033 1D10F76F FC01E013 6657DF97 319ABEEF 6BD52937 4B810C03 338001E7
  //   7B10603 BC00867 8267E17 4CB78F6F 1AC00E67 EC006E7 1A351BEF 42800CE7 F0AEE713 75C005E7 EE44FB37
  //   5D99476F 53310183 65810823 2A4751EF 15310503 77975EEF 70510083 1EC00E67 39CDE213 48610783 AD10883
  //   6A9EF4B7 6F010D23 AF75E8B7 28A10183 25000A67 1F0BF313 A794C013 B4EEEEF 2A400967 1C2E2B3 29310BA3
  //   55BB3CEF 48110E03 17C109A3 64D60BEF 18CE2B7 5AC10A83 432F893 2A0001E7 DFE377B7 6E75896F 2D000467
  //   B94EB3 A544E737 4E4002E7 7EFB3 99D79EF 290002E7 17400767 56C006E7 11F13DEF 2148E6EF 57D10823
  //   15C00467 50710C23 40850BB3 23854EF EA10B6F 7B800A67 6A610503 24C00B67 64110323 3989B3 14773B3
  //   701F966F 85FFD197 8A1F0313 3F110723 6EFB946F 682484EF 359FCB93 75710903 7F800AE7 70A8B36F 6DA10DA3
  //   70FD9E17 C7BFF793 26400C67 1307286F 54000067 2B09E46F 34C005E7 C0D4613 584001E7 1780DB3 15210703
  //   272DC6EF 91AC18B7 82976093 54A524B7 2E410B83 23000367 42C00267 DC6E33 3900CB3 613103A3 309C7EF
  //   3F69DB3 7083E4EF 4180F13 22C100A3 938A6193 3349D2EF 18F80DEF 3B3A086F 2938C33 3F910B03 A689CB93
  //   21B09797 B400BE7 728106A3 F1BED5B7 A2F2313 39410683 23933B3 18A9033 668007E7 8F11C397 463102A3
  //   4E5101A3 32C10DA3 27A433 5AD25197 956E3CB7 298100A3 7710503 38B1D917 61F6ECEF 67400667 1B400367
  //   9FA86B13 12C10FA3 EB99F913 2B411B3 26000267 16400FE7 93E0A793 DA547213 1E000A67 61C00367 D2AFE493
  //   1C400E67 6FF107A3 9D6433 10427213 32A10183 62010A83 52CDB3 59A6CB97 16EE8DEF 3521D6F 2F110283
  //   1B34F33 44800367 10E104A3 30410083 2B810CA3 13C2833 1F000567 272C476F 62C007E7 1E400CE7 24C00967
  //   29871937 70010B23 14B52E13 2327F7EF 4CA6B3 17A8466F 393F25EF 64F10783 11FC033 5C8DB3 26C601EF
  //   5610B23 42F10C23 5502736F 54400CE7 676B366F 47A500EF A5C2DC17 21400567 49C00367 735D0313 5A0001E7
  //   5078C613 878233 6E400B67 6D41B6EF B6858EF F9DC017 4D910623 6CE1E497 70810403 15BD0513 718105A3
  //   D297CB13 EAA6FB7 44F10403 9B25FB13 3763633 6B510883 2DE103A3 1C67B33 323B0B3 1D000F67 20010023
  //   A9190C37 6D04B237 5AF10C03 9010A83 B94EC013 3A000C67 229655EF 2EC55D6F 52C00BE7 384002E7 C35ACD93
  //   45E519EF 664002E7 EBF793 7EC007E7 3AD669EF 59800467 58110483 53363EF 5D0A806F A80F4CB7 190EAB6F
  //   68400CE7 4562FA13 62710D03 385B233 3F810B03 3CCFAF6F 5575456F 4B810183 230DEB6F F000367 69C00B67
  //   754102A3 2310983 F8403217 63E8A593 17810383 268004E7 1AE9A56F 456EE9EF 338003E7 10310023 1CBC233
  //   763C2A93 779C3F6F 1CEE506F 458DC26F 881EA197 11F10CA3 77A10D83 7B0EBFEF 81AD4D17 763D6FB7 64A10883
  //   64676993 8680FC13 7E010583 2523FB3 41C10DA3 18BA5B6F 6BB10883 30410F83 8800567 1C800A67 583584EF
  //   2A64413 330F19EF 34D15B3 25ACAAEF 4DEB33 72F8C46F 42000EE7 5B7569EF 337102A3 37CC0B13 B63E6593
  //   649100A3 3549A33 60710683 26110283 58400767 35B102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
  //   Instruction Memory
  //   Halts Execution After Constant # of Clock Cycles
  //   Constant
endmodule
